// Logisim project ProjectDraft1.circ as structural Verilog: 1 circuit, main circuit main
module main (
  input  A,
  input  B,
  input  C,
  input  D,
  output out_5,
  output out_6
);

  wire xor_1_out, xor_2_out;

  xor xor_1 (xor_1_out, A, B);
  xor xor_2 (xor_2_out, xor_1_out, C);
  xor xor_3 (out_5, xor_2_out, D);
  not not_1 (out_6, out_5);

  // Notes on the sheet:
  //   X1
  //   X2
  //   Even_parity_correction bit
  //   Odd_parity_correction bit
endmodule
